// Logisim project Prac5.circ as structural Verilog: 6 circuits, main circuit Adder/Subtractor
module main (
  input  A0,
  input  B0,
  input  A1,
  input  B1,
  input  F0,
  input  F1,
  input  F2,
  output out_8,
  output out_9,
  output out_10,
  output out_11,
  output out_12
);

  wire Adder_Subtractor_p2, Adder_Subtractor_p3, Adder_Subtractor_p4;

  BitAND bitand_1 (.A0(A0), .B0(B0), .A1(A1), .B1(B1), .Y0(out_9), .Y1(out_11));
  // Adder_Subtractor Adder_Subtractor: pin names not known; wires that end beside it: A0, Adder_Subtractor_p2, Adder_Subtractor_p3, Adder_Subtractor_p4, F0, out_8, out_10, out_12

  // Notes on the sheet:
  //   for increment set b1b0 to 01 and cho0se slect line for + or -
endmodule

module Adder_Subtractor (
  input  A0,
  input  B0,
  input  Sel,
  input  A1,
  input  B1,
  output S0,
  output S1,
  output Cout
);

  wire adder_1_cout, xor_1_out, xor_2_out;

  xor xor_1 (xor_1_out, B0, Sel);
  xor xor_2 (xor_2_out, B1, Sel);
  Adder #(.width(1)) adder_1 (.a(A0), .b(xor_1_out), .out(S0), .cin(Sel), .cout(adder_1_cout));
  Adder #(.width(1)) adder_2 (.a(A1), .b(xor_2_out), .out(S1), .cin(adder_1_cout), .cout(Cout));

  // Notes on the sheet:
  //   Sel=0:adder
  //   Sel=1:subtractor
endmodule

module BitAND (
  input  A0,
  input  B0,
  input  A1,
  input  B1,
  output Y0,
  output Y1
);

  and and_1 (Y0, A0, B0);
  and and_2 (Y1, A1, B1);
endmodule

module bitOR (
  input  A0,
  input  B0,
  input  A1,
  input  B1,
  output Y0,
  output Y1
);

  or or_1 (Y0, A0, B0);
  or or_2 (Y1, A1, B1);
endmodule

module Multiplyx2 (
  input  A1,
  input  A0,
  output Y1,
  output Y0
);

  Multiplexer #(.enable("false")) multiplexer_1 (.in0(A1), .in1(A0), .out(Y1), .sel(1'b1));
  Multiplexer #(.enable("false")) multiplexer_2 (.in0(A0), .in1(1'b0), .out(Y0), .sel(1'b1));
endmodule

module Divide_2 (
  input  A1,
  input  A0,
  output Y0,
  output Y1
);

  Multiplexer #(.enable("false")) multiplexer_1 (.in0(A0), .in1(A1), .out(Y0), .sel(1'b1));
  Multiplexer #(.enable("false")) multiplexer_2 (.in0(A1), .in1(1'b0), .out(Y1), .sel(1'b1));
endmodule
